# Fritzing sketch Schematic (saved by Fritzing 0.9.9b)
breadboards: 1

parts:
  Part1 = Arduino Uno (Rev3)
  S1 = Pushbutton [package="[THT]"]
  S2 = Pushbutton [package="[THT]"]
  J1 = Piezo Speaker
  LCD1 = LCD screen
  LCM1602_IIC1 = LCM1602 IIC [part_number="LCM1602 IIC" chip_label="LCM1602 IIC" package="DIP (Dual Inline) [THT]"]
  Part2 = Thumb Joystick
  BATT2 = 3xAAA Switchable Battery Pack w/Bare Wire
  C1 = Capacitor Polarized [package=cpol-radial-1000uf-25v]
  NEOPIXEL9 = Neopixel Strip -- Black (60/m) [part_number=1461]
  J2 = female pin header, 3 pins [form="♀ (female)"]
  J3 = female pin header, 3 pins [form="♀ (female)"]

nets:
  N1: Part1.A0, Part2.VERT
  N2: Part1.A1, Part2.HORZ
  N3: Part1.A4/SDA, LCM1602_IIC1.SDA
  N4: Part1.A5/SCL, LCM1602_IIC1.SCL
  GND: Part1.GND, S1.Pin_1, S1.Pin_2, S2.Pin_1, S2.Pin_2, J1.pin1, LCD1.VSS, LCM1602_IIC1.VSS, LCM1602_IIC1.GND, Part2.GND
  N5: Part1.D2, NEOPIXEL9.DI
  N6: Part1.D3_PWM, J1.pin2
  N7: Part1.D4, S2.Pin_3, S2.Pin_4
  N8: Part1.D5_PWM, S1.Pin_3, S1.Pin_4
  VCC: Part1.5V, LCM1602_IIC1.VCC, Part2.VCC
  VDD: LCD1.VDD, LCM1602_IIC1.VDD
  N9: LCD1.V0, LCM1602_IIC1.V0
  N10: LCD1.RS, LCM1602_IIC1.RS
  N11: LCD1.R/W, LCM1602_IIC1.RW
  N12: LCD1.E, LCM1602_IIC1.E
  N13: LCD1.DB0, LCM1602_IIC1.D0
  N14: LCD1.DB1, LCM1602_IIC1.D1
  N15: LCD1.DB2, LCM1602_IIC1.D2
  N16: LCD1.DB3, LCM1602_IIC1.D3
  N17: LCD1.DB4, LCM1602_IIC1.D4
  N18: LCD1.DB5, LCM1602_IIC1.D5
  N19: LCD1.DB6, LCM1602_IIC1.D6
  N20: LCD1.DB7, LCM1602_IIC1.D7
  N21: LCD1.LED+, LCM1602_IIC1.A
  N22: LCD1.LED-, LCM1602_IIC1.K
  N23: LCM1602_IIC1.LED_A, LCM1602_IIC1.LED_B
  N24: BATT2.POS, J3.pin1
  N25: BATT2.NEG, J2.pin1
  N26: C1.+, J3.pin2
  N27: C1.-, J2.pin2
  N28: NEOPIXEL9.+5V, J3.pin3
  N29: NEOPIXEL9.GND, J2.pin3

custom parts:
  LCM1602 IIC: I2C-Module to use a 1602 or 2004 LCD on with the wire.h libory Serial LCD Modul
  3xAAA Switchable Battery Pack w/Bare Wire: 3xAAA Switchable Battery Pack w/Bare Wire Connectors
  Neopixel Strip -- Black (60/m): Neopixel Strip, Black, 60 pixels per meter.
